// Logisim project first DLD assignment second semester.circ as structural Verilog: 1 circuit, main circuit main
module main (
  output out_1,
  output out_2,
  output out_3,
  output C
);

  wire and_1_out, and_2_out, undriven, undriven_2, undriven_3, undriven_4, undriven_5, undriven_6,
       undriven_7, undriven_8, undriven_9, undriven_10, undriven_11, undriven_12, undriven_13, undriven_14,
       undriven_15, undriven_16, undriven_17, undriven_18, undriven_19;
  wire [2:0] priority_encoder_1_out;

  // OR_Gate or_1 has open pins: in1=undriven_3, in2=undriven_4, in4=undriven_5, out=open
  and and_1 (and_1_out, out_2, undriven);
  buf and_2 (and_2_out, undriven_2);  // AND_Gate
  // OR_Gate or_2 has open pins: in0=undriven_6, in2=undriven_7, in4=undriven_8, out=open
  // OR_Gate or_3 has open pins: in0=and_1_out, in3=and_2_out, out=open
  // AND_Gate and_3 has open pins: in0=out_1, in1=undriven_9, in2=undriven_17, out=open
  // OR_Gate or_4 has open pins: in1=undriven_17, out=open
  Priority_Encoder priority_encoder_1 (
    .in0(undriven_10), .in1(undriven_11), .in2(undriven_12), .in3(undriven_13), .in4(undriven_14),
    .in5(undriven_15), .in6(undriven_18), .in7(undriven_16), .out(priority_encoder_1_out), .en_in(undriven_19));  // open: gs, en_out
  // OR_Gate or_5 has open pins: in0=out_1, in1=out_1, out=open

  // Notes on the sheet:
  //   Answer .1:
  //   Answer .2:
  //   Answer 3:
  //   Aziz Ahmad Afzali
  //   ID:201-2204033
  //   A
  //   B
  //   A
  //   B
  //   A
  //   B
  //   C
  //   A
  //   B
  //   C
  //   Answer 4:
  //   A
  //   B
  //   C
  //   A
  //   I1
  //   Answer 5:
  //   i2
  //   i3
  //   i4
  //   i5
  //   i6
  //   i7
  //   i8
  //   M
  //   O
endmodule
